// Logisim project ULA.circ as structural Verilog
module op_ADD (
  input  in_1,
  input  in_2,
  input  Carry_In,
  output out_4,
  output out_5
);

  wire and_1_out, and_2_out, xor_1_out;

  xor xor_1 (xor_1_out, in_2, in_1);
  and and_1 (and_1_out, in_2, in_1);
  and and_2 (and_2_out, xor_1_out, Carry_In);
  xor xor_2 (out_4, xor_1_out, Carry_In);
  or or_1 (out_5, and_2_out, and_1_out);

  // Notes on the sheet:
  //   Resultado
  //   Carry Out
endmodule

module op_NOR (
  input  in_1,
  input  in_2,
  output out_3
);

  nor nor_1 (out_3, in_1, in_2);
endmodule

module op_OR (
  input  in_1,
  input  in_2,
  output out_3
);

  or or_1 (out_3, in_1, in_2);
endmodule

module op_NAND (
  input  in_1,
  input  in_2,
  output out_3
);

  nand nand_1 (out_3, in_1, in_2);
endmodule

module mux_8x1 (
  input  [7:0] in_1,
  input  [7:0] in_2,
  input  [7:0] in_3,
  input  [7:0] in_4,
  input  [7:0] in_5,
  input  [7:0] in_6,
  input  [7:0] in_7,
  input  [7:0] in_8
);
endmodule

module ula (
  input  [7:0] in_1,
  input  [7:0] in_2
);

  Multiplier multiplier_1 (.a(in_1), .b(in_2));  // open: out, cin, cout
  Divider divider_1 (.a(in_1), .b(in_2));  // open: out, upper, rem
  ula_NOR ula_nor_1 (.in_1(in_1), .in_2(in_2));  // open: out_3
  ula_ADD ula_add_1 (.in_1(in_1), .in_2(in_2));  // open: out_3
  ula_NAND ula_nand_1 (.in_1(in_1), .in_2(in_2));  // open: out_3
  ula_SUB ula_sub_1 (.in_1(in_1), .in_2(in_2));  // open: out_3
  ula_OR ula_or_1 (.in_1(in_1), .in_2(in_2));  // open: out_3
  ula_OR ula_or_2 (.in_1(in_1), .in_2(in_2));  // open: out_3

  // Notes on the sheet:
  //   implementar saídas Z, C, e MUX
endmodule

module ula_ADD (
  input  [7:0] in_1,
  input  [7:0] in_2,
  output [7:0] out_3
);

  wire op_add_1_out_5, op_add_2_out_5, op_add_3_out_5, op_add_4_out_5, op_add_5_out_5, op_add_6_out_5,
       op_add_7_out_5;

  op_ADD op_add_1 (.in_1(in_1[0]), .in_2(in_2[0]), .out_4(out_3[0]), .out_5(op_add_1_out_5));  // open: Carry_In
  op_ADD op_add_2 (.in_1(in_1[1]), .in_2(in_2[1]), .Carry_In(op_add_1_out_5), .out_4(out_3[1]), .out_5(op_add_2_out_5));
  op_ADD op_add_3 (.in_1(in_1[2]), .in_2(in_2[2]), .Carry_In(op_add_2_out_5), .out_4(out_3[2]), .out_5(op_add_3_out_5));
  op_ADD op_add_4 (.in_1(in_1[3]), .in_2(in_2[3]), .Carry_In(op_add_3_out_5), .out_4(out_3[3]), .out_5(op_add_4_out_5));
  op_ADD op_add_5 (.in_1(in_1[4]), .in_2(in_2[4]), .Carry_In(op_add_4_out_5), .out_4(out_3[4]), .out_5(op_add_5_out_5));
  op_ADD op_add_6 (.in_1(in_1[5]), .in_2(in_2[5]), .Carry_In(op_add_5_out_5), .out_4(out_3[5]), .out_5(op_add_6_out_5));
  op_ADD op_add_7 (.in_1(in_1[6]), .in_2(in_2[6]), .Carry_In(op_add_6_out_5), .out_4(out_3[6]), .out_5(op_add_7_out_5));
  op_ADD op_add_8 (.in_1(in_1[7]), .in_2(in_2[7]), .Carry_In(op_add_7_out_5), .out_4(out_3[7]));  // open: out_5

  // Notes on the sheet:
  //   IMPLEMENTAR OVERFLOW
endmodule

module ula_NOR (
  input  [7:0] in_1,
  input  [7:0] in_2,
  output [7:0] out_3
);

  op_NOR op_nor_1 (.in_1(in_1[0]), .in_2(in_2[0]), .out_3(out_3[0]));
  op_NOR op_nor_2 (.in_1(in_1[1]), .in_2(in_2[1]), .out_3(out_3[1]));
  op_NOR op_nor_3 (.in_1(in_1[2]), .in_2(in_2[2]), .out_3(out_3[2]));
  op_NOR op_nor_4 (.in_1(in_1[3]), .in_2(in_2[3]), .out_3(out_3[3]));
  op_NOR op_nor_5 (.in_1(in_1[4]), .in_2(in_2[4]), .out_3(out_3[4]));
  op_NOR op_nor_6 (.in_1(in_1[5]), .in_2(in_2[5]), .out_3(out_3[5]));
  op_NOR op_nor_7 (.in_1(in_1[6]), .in_2(in_2[6]), .out_3(out_3[6]));
  op_NOR op_nor_8 (.in_1(in_1[7]), .in_2(in_2[7]), .out_3(out_3[7]));
endmodule

module ula_OR (
  input  [7:0] in_1,
  input  [7:0] in_2,
  output [7:0] out_3
);

  op_OR op_or_1 (.in_1(in_1[0]), .in_2(in_2[0]), .out_3(out_3[0]));
  op_OR op_or_2 (.in_1(in_1[1]), .in_2(in_2[1]), .out_3(out_3[1]));
  op_OR op_or_3 (.in_1(in_1[2]), .in_2(in_2[2]), .out_3(out_3[2]));
  op_OR op_or_4 (.in_1(in_1[3]), .in_2(in_2[3]), .out_3(out_3[3]));
  op_OR op_or_5 (.in_1(in_1[4]), .in_2(in_2[4]), .out_3(out_3[4]));
  op_OR op_or_6 (.in_1(in_1[5]), .in_2(in_2[5]), .out_3(out_3[5]));
  op_OR op_or_7 (.in_1(in_1[6]), .in_2(in_2[6]), .out_3(out_3[6]));
  op_OR op_or_8 (.in_1(in_1[7]), .in_2(in_2[7]), .out_3(out_3[7]));
endmodule

module ula_NAND (
  input  [7:0] in_1,
  input  [7:0] in_2,
  output [7:0] out_3
);

  op_NAND op_nand_1 (.in_1(in_1[0]), .in_2(in_2[0]), .out_3(out_3[0]));
  op_NAND op_nand_2 (.in_1(in_1[1]), .in_2(in_2[1]), .out_3(out_3[1]));
  op_NAND op_nand_3 (.in_1(in_1[2]), .in_2(in_2[2]), .out_3(out_3[2]));
  op_NAND op_nand_4 (.in_1(in_1[3]), .in_2(in_2[3]), .out_3(out_3[3]));
  op_NAND op_nand_5 (.in_1(in_1[4]), .in_2(in_2[4]), .out_3(out_3[4]));
  op_NAND op_nand_6 (.in_1(in_1[5]), .in_2(in_2[5]), .out_3(out_3[5]));
  op_NAND op_nand_7 (.in_1(in_1[6]), .in_2(in_2[6]), .out_3(out_3[6]));
  op_NAND op_nand_8 (.in_1(in_1[7]), .in_2(in_2[7]), .out_3(out_3[7]));
endmodule

module ula_SUB (
  input  [7:0] in_1,
  input  [7:0] in_2,
  output [7:0] out_3
);

  wire not_1_out, not_2_out, not_3_out, not_4_out, not_5_out, not_6_out, not_7_out, not_8_out,
       op_add_1_out_5, op_add_2_out_5, op_add_3_out_5, op_add_4_out_5, op_add_5_out_5, op_add_6_out_5,
       op_add_7_out_5;

  not not_1 (not_1_out, in_2[0]);
  not not_2 (not_2_out, in_2[1]);
  not not_3 (not_3_out, in_2[2]);
  not not_4 (not_4_out, in_2[3]);
  not not_5 (not_5_out, in_2[4]);
  not not_6 (not_6_out, in_2[5]);
  not not_7 (not_7_out, in_2[6]);
  not not_8 (not_8_out, in_2[7]);
  op_ADD op_add_1 (.in_1(in_1[0]), .in_2(not_1_out), .Carry_In(1'b1), .out_4(out_3[0]), .out_5(op_add_1_out_5));
  op_ADD op_add_2 (
    .in_1(in_1[1]), .in_2(not_2_out), .Carry_In(op_add_1_out_5), .out_4(out_3[1]), .out_5(op_add_2_out_5));
  op_ADD op_add_3 (
    .in_1(in_1[2]), .in_2(not_3_out), .Carry_In(op_add_2_out_5), .out_4(out_3[2]), .out_5(op_add_3_out_5));
  op_ADD op_add_4 (
    .in_1(in_1[3]), .in_2(not_4_out), .Carry_In(op_add_3_out_5), .out_4(out_3[3]), .out_5(op_add_4_out_5));
  op_ADD op_add_5 (
    .in_1(in_1[4]), .in_2(not_5_out), .Carry_In(op_add_4_out_5), .out_4(out_3[4]), .out_5(op_add_5_out_5));
  op_ADD op_add_6 (
    .in_1(in_1[5]), .in_2(not_6_out), .Carry_In(op_add_5_out_5), .out_4(out_3[5]), .out_5(op_add_6_out_5));
  op_ADD op_add_7 (
    .in_1(in_1[6]), .in_2(not_7_out), .Carry_In(op_add_6_out_5), .out_4(out_3[6]), .out_5(op_add_7_out_5));
  op_ADD op_add_8 (.in_1(in_1[7]), .in_2(not_8_out), .Carry_In(op_add_7_out_5), .out_4(out_3[7]));  // open: out_5

  // Notes on the sheet:
  //   IMPLEMENTAR OVERFLOW
endmodule
